// Logisim project calculator.circ as structural Verilog: 13 circuits, main circuit left-right shift register is falling edge triggered! (24/12/2011 6:46PM A'bad)
module left_right_shift_register_is_falling_edge_triggered___24_12_2011_6_46PM_A_bad (
  input  ADDITION,
  input  SUBTRACTION,
  input  MULTIPLICATION,
  input  DIVISION
);

  wire _0_2_out, _0_3_out, _0_4_out, _0_5_out, _0_7_out, _0_8_out, _0_9_out, _0_10_out, _1_2_out, _1_3_out,
       _1_4_out, _1_5_out, _1_7_out, _1_8_out, _1_9_out, _1_10_out, and_1_out, and_2_out, Backspace,
       Backspace_m, Clear_All, Clear_All_m, CLOCK, CLOCK_m, m0, m1, m2, m3, m4, m5, m6, m7, m8, m9, n0, n1,
       n2, n3, n4, n5, n6, n7, n8, n9, not_1_out, not_2_out, or_1_out, or_2_out, or_3_out, or_4_out,
       or_5_out, or_6_out, or_7_out, or_8_out, or_9_out, or_10_out, or_11_out, or_12_out, or_13_out,
       or_14_out, or_16_out, or_17_out, or_18_out, or_19_out, or_20_out, or_21_out, or_22_out, or_23_out,
       or_24_out, or_25_out, or_26_out, or_27_out, or_28_out, or_29_out, or_32_out, t_ff_1_q, t_ff_1_qn,
       t_ff_2_q, t_ff_2_qn, t_ff_3_q, t_ff_3_qn, t_ff_4_q, t_ff_4_qn, t_ff_5_q, t_ff_5_qn, t_ff_6_q,
       t_ff_6_qn, t_ff_7_q, t_ff_7_qn, t_ff_8_q, t_ff_8_qn;
  wire [1:0] and_3_out;
  wire [3:0] _0m, _0n, _1m, _1n, _2m, _2n, _3m, _3n, bcd_adder_1_o0, bcd_adder_1_o1, bcd_adder_1_o2,
       bcd_adder_1_o3, bcd_adder_1_o4, bcd_adder_1_o5, bcd_adder_1_o6, bcd_adder_1_o7, bcd_division_1_o0,
       bcd_division_1_o1, bcd_division_1_o2, bcd_division_1_o3, bcd_division_1_o4, bcd_division_1_o5,
       bcd_division_1_o6, bcd_division_1_o7, bcd_division_1_r0, bcd_division_1_r1, bcd_division_1_r2,
       bcd_division_1_r3, bcd_multiplication_1_o0, bcd_multiplication_1_o1, bcd_multiplication_1_o2,
       bcd_multiplication_1_o3, bcd_multiplication_1_o4, bcd_multiplication_1_o5, bcd_multiplication_1_o6,
       bcd_multiplication_1_o7, bcd_subtractor_1_o0, bcd_subtractor_1_o1, bcd_subtractor_1_o2,
       bcd_subtractor_1_o3, bcd_subtractor_1_o4, bcd_subtractor_1_o5, bcd_subtractor_1_o6,
       bcd_subtractor_1_o7, O0, O1, O2, O3, O4, O5, O6, O7, R0, R1, R2, R3;
  wire [11:4] bit0, bit0_m, bit1, bit1_m, bit2, bit2_m, bit3, bit3_m;

  Hex_Digit_Display hex_digit_display_1 (.value(_3n));  // open: dp
  or or_1 (or_1_out, n8, n6, n4, n2, n0);
  or or_2 (or_2_out, n9, n7, n5, n3, n1);
  or or_3 (or_3_out, n9, n8, n5, n4, n1, n0);
  or or_4 (or_4_out, n7, n6, n3, n2);
  or or_5 (or_5_out, n9, n8, n3, n2, n1, n0);
  or or_6 (or_6_out, n7, n6, n5, n4);
  or or_7 (or_7_out, n7, n6, n5, n4, n3, n2, n1, n0);
  or or_8 (or_8_out, n9, n8);
  Hex_Digit_Display hex_digit_display_2 (.value(_2n));  // open: dp
  Hex_Digit_Display hex_digit_display_3 (.value(_1n));  // open: dp
  Button _8 (.out(n8));
  Button _7 (.out(n7));
  Button _5 (.out(n5));
  Button _4 (.out(n4));
  Button _1 (.out(n1));
  Button _2 (.out(n2));
  Button _0 (.out(n0));
  or or_9 (or_9_out, _3n[0], _3n[1], _3n[2], _3n[3]);
  and _0_2 (_0_2_out, or_1_out, t_ff_1_q);
  and _1_2 (_1_2_out, t_ff_1_qn, or_2_out);
  and _0_3 (_0_3_out, or_3_out, t_ff_2_q);
  and _1_3 (_1_3_out, t_ff_2_qn, or_4_out);
  and _0_4 (_0_4_out, or_5_out, t_ff_3_q);
  and _1_4 (_1_4_out, t_ff_3_qn, or_6_out);
  and _0_5 (_0_5_out, or_7_out, t_ff_4_q);
  and _1_5 (_1_5_out, t_ff_4_qn, or_8_out);
  Hex_Digit_Display hex_digit_display_4 (.value(_0n));  // open: dp
  Button _9 (.out(n9));
  Button _6 (.out(n6));
  Button _3 (.out(n3));
  Button button (.out(Backspace));
  Button CE (.out(Clear_All));
  or or_10 (or_10_out, n0, n1, n2, n3, n4, n5, n6, n7, n8, n9);
  or or_11 (or_11_out, _0_2_out, _1_2_out);
  T_Flip_Flop t_ff_1 (.clk(or_11_out), .T(1'b1), .Q(t_ff_1_q), .Qn(t_ff_1_qn));  // open: preset, reset, en
  T_Flip_Flop t_ff_2 (.clk(or_12_out), .T(1'b1), .Q(t_ff_2_q), .Qn(t_ff_2_qn));  // open: preset, reset, en
  or or_12 (or_12_out, _0_3_out, _1_3_out);
  T_Flip_Flop t_ff_3 (.clk(or_13_out), .T(1'b1), .Q(t_ff_3_q), .Qn(t_ff_3_qn));  // open: preset, reset, en
  or or_13 (or_13_out, _0_4_out, _1_4_out);
  or or_14 (or_14_out, _0_5_out, _1_5_out);
  T_Flip_Flop t_ff_4 (.clk(or_14_out), .T(1'b1), .Q(t_ff_4_q), .Qn(t_ff_4_qn));  // open: preset, reset, en
  and and_1 (and_1_out, or_10_out, ~or_9_out);  // AND_Gate
  _12_bit_left_right_shift_register LSB (
    .Data_in_right_shift(t_ff_1_q), .right_left_shift(Backspace), .CLK(CLOCK),
    .Current_State__12_bits({bit0, _3n[0], _2n[0], _1n[0], _0n[0]}), .RESET(Clear_All));
  _12_bit_left_right_shift_register u_12_bit_left_right_shift_register_1 (
    .Data_in_right_shift(t_ff_2_q), .right_left_shift(Backspace), .CLK(CLOCK),
    .Current_State__12_bits({bit1, _3n[1], _2n[1], _1n[1], _0n[1]}), .RESET(Clear_All));
  _12_bit_left_right_shift_register u_12_bit_left_right_shift_register_2 (
    .Data_in_right_shift(t_ff_3_q), .right_left_shift(Backspace), .CLK(CLOCK),
    .Current_State__12_bits({bit2, _3n[2], _2n[2], _1n[2], _0n[2]}), .RESET(Clear_All));
  _12_bit_left_right_shift_register MSB (
    .Data_in_right_shift(t_ff_4_q), .right_left_shift(Backspace), .CLK(CLOCK),
    .Current_State__12_bits({bit3, _3n[3], _2n[3], _1n[3], _0n[3]}), .RESET(Clear_All));
  or or_15 (CLOCK, and_1_out, Backspace);
  Hex_Digit_Display hex_digit_display_5 (.value(_3m));  // open: dp
  Hex_Digit_Display hex_digit_display_6 (.value(_2m));  // open: dp
  Button _7_2 (.out(m7));
  Button _4_2 (.out(m4));
  Button _1_6 (.out(m1));
  Button _0_6 (.out(m0));
  Hex_Digit_Display hex_digit_display_7 (.value(_1m));  // open: dp
  Hex_Digit_Display hex_digit_display_8 (.value(_0m));  // open: dp
  Button _8_2 (.out(m8));
  Button _9_2 (.out(m9));
  Button _5_2 (.out(m5));
  Button _6_2 (.out(m6));
  Button _2_2 (.out(m2));
  Button _3_2 (.out(m3));
  Button CE_2 (.out(Clear_All_m));
  Button button_2 (.out(Backspace_m));
  or or_16 (or_16_out, m8, m6, m4, m2, m0);
  and _0_7 (_0_7_out, or_16_out, t_ff_5_q);
  and _1_7 (_1_7_out, t_ff_5_qn, or_17_out);
  or or_17 (or_17_out, m9, m7, m5, m3, m1);
  or or_18 (or_18_out, m9, m8, m5, m4, m1, m0);
  and _0_8 (_0_8_out, or_18_out, t_ff_6_q);
  and _1_8 (_1_8_out, t_ff_6_qn, or_19_out);
  or or_19 (or_19_out, m7, m6, m3, m2);
  or or_20 (or_20_out, m9, m8, m3, m2, m1, m0);
  and _0_9 (_0_9_out, or_20_out, t_ff_7_q);
  and _1_9 (_1_9_out, t_ff_7_qn, or_21_out);
  or or_21 (or_21_out, m7, m6, m5, m4);
  or or_22 (or_22_out, m7, m6, m5, m4, m3, m2, m1, m0);
  and _0_10 (_0_10_out, or_22_out, t_ff_8_q);
  and _1_10 (_1_10_out, t_ff_8_qn, or_23_out);
  or or_23 (or_23_out, m9, m8);
  or or_24 (or_24_out, m0, m1, m2, m3, m4, m5, m6, m7, m8, m9);
  or or_25 (or_25_out, _3m[0], _3m[1], _3m[2], _3m[3]);
  or or_26 (or_26_out, _0_7_out, _1_7_out);
  or or_27 (or_27_out, _0_8_out, _1_8_out);
  or or_28 (or_28_out, _0_9_out, _1_9_out);
  or or_29 (or_29_out, _0_10_out, _1_10_out);
  and and_2 (and_2_out, or_24_out, ~or_25_out);  // AND_Gate
  T_Flip_Flop t_ff_5 (.clk(or_26_out), .T(1'b1), .Q(t_ff_5_q), .Qn(t_ff_5_qn));  // open: preset, reset, en
  T_Flip_Flop t_ff_6 (.clk(or_27_out), .T(1'b1), .Q(t_ff_6_q), .Qn(t_ff_6_qn));  // open: preset, reset, en
  T_Flip_Flop t_ff_7 (.clk(or_28_out), .T(1'b1), .Q(t_ff_7_q), .Qn(t_ff_7_qn));  // open: preset, reset, en
  T_Flip_Flop t_ff_8 (.clk(or_29_out), .T(1'b1), .Q(t_ff_8_q), .Qn(t_ff_8_qn));  // open: preset, reset, en
  or or_30 (CLOCK_m, and_2_out, Backspace_m);
  _12_bit_left_right_shift_register LSB_2 (
    .Data_in_right_shift(t_ff_5_q), .right_left_shift(Backspace_m), .CLK(CLOCK_m),
    .Current_State__12_bits({bit0_m, _3m[0], _2m[0], _1m[0], _0m[0]}), .RESET(Clear_All_m));
  _12_bit_left_right_shift_register u_12_bit_left_right_shift_register_3 (
    .Data_in_right_shift(t_ff_6_q), .right_left_shift(Backspace_m), .CLK(CLOCK_m),
    .Current_State__12_bits({bit1_m, _3m[1], _2m[1], _1m[1], _0m[1]}), .RESET(Clear_All_m));
  _12_bit_left_right_shift_register u_12_bit_left_right_shift_register_4 (
    .Data_in_right_shift(t_ff_7_q), .right_left_shift(Backspace_m), .CLK(CLOCK_m),
    .Current_State__12_bits({bit2_m, _3m[2], _2m[2], _1m[2], _0m[2]}), .RESET(Clear_All_m));
  _12_bit_left_right_shift_register MSB_2 (
    .Data_in_right_shift(t_ff_8_q), .right_left_shift(Backspace_m), .CLK(CLOCK_m),
    .Current_State__12_bits({bit3_m, _3m[3], _2m[3], _1m[3], _0m[3]}), .RESET(Clear_All_m));
  Hex_Digit_Display hex_digit_display_9 (.value(O7));  // open: dp
  Hex_Digit_Display hex_digit_display_10 (.value(O6));  // open: dp
  Hex_Digit_Display hex_digit_display_11 (.value(O5));  // open: dp
  Hex_Digit_Display hex_digit_display_12 (.value(R3));  // open: dp
  Hex_Digit_Display hex_digit_display_13 (.value(R2));  // open: dp
  Hex_Digit_Display hex_digit_display_14 (.value(O4));  // open: dp
  Hex_Digit_Display hex_digit_display_15 (.value(O3));  // open: dp
  Hex_Digit_Display hex_digit_display_16 (.value(R0));  // open: dp
  Hex_Digit_Display hex_digit_display_17 (.value(R1));  // open: dp
  Hex_Digit_Display hex_digit_display_18 (.value(O2));  // open: dp
  Hex_Digit_Display hex_digit_display_19 (.value(O1));  // open: dp
  Hex_Digit_Display hex_digit_display_20 (.value(O0));  // open: dp
  BCD_Adder bcd_adder_1 (
    ._0n(_0n), ._1n(_1n), ._2n(_2n), ._3n(_3n), ._0m(_0m), ._1m(_1m), ._2m(_2m), ._3m(_3m),
    .O0(bcd_adder_1_o0), .O1(bcd_adder_1_o1), .O2(bcd_adder_1_o2), .O3(bcd_adder_1_o3), .O4(bcd_adder_1_o4),
    .O5(bcd_adder_1_o5), .O6(bcd_adder_1_o6), .O7(bcd_adder_1_o7));
  BCD_subtractor bcd_subtractor_1 (
    ._0n(_0n), ._1n(_1n), ._2n(_2n), ._3n(_3n), ._0m(_0m), ._1m(_1m), ._2m(_2m), ._3m(_3m),
    .O0(bcd_subtractor_1_o0), .O1(bcd_subtractor_1_o1), .O2(bcd_subtractor_1_o2), .O3(bcd_subtractor_1_o3),
    .O4(bcd_subtractor_1_o4), .O5(bcd_subtractor_1_o5), .O6(bcd_subtractor_1_o6), .O7(bcd_subtractor_1_o7));
  BCD_multiplication bcd_multiplication_1 (
    ._0n(_0n), ._1n(_1n), ._2n(_2n), ._3n(_3n), ._0m(_0m), ._1m(_1m), ._2m(_2m), ._3m(_3m),
    .O0(bcd_multiplication_1_o0), .O1(bcd_multiplication_1_o1), .O2(bcd_multiplication_1_o2),
    .O3(bcd_multiplication_1_o3), .O4(bcd_multiplication_1_o4), .O5(bcd_multiplication_1_o5),
    .O6(bcd_multiplication_1_o6), .O7(bcd_multiplication_1_o7));
  BCD_division bcd_division_1 (
    ._0n(_0n), ._1n(_1n), ._2n(_2n), ._3n(_3n), ._0m(_0m), ._1m(_1m), ._2m(_2m), ._3m(_3m),
    .O0(bcd_division_1_o0), .O1(bcd_division_1_o1), .O2(bcd_division_1_o2), .O3(bcd_division_1_o3),
    .O4(bcd_division_1_o4), .O5(bcd_division_1_o5), .O6(bcd_division_1_o6), .O7(bcd_division_1_o7),
    .R0(bcd_division_1_r0), .R1(bcd_division_1_r1), .R2(bcd_division_1_r2), .R3(bcd_division_1_r3));
  Multiplexer #(.select(2), .width(32)) multiplexer_1 (
    .in0({bcd_adder_1_o7, bcd_adder_1_o6, bcd_adder_1_o5, bcd_adder_1_o4, bcd_adder_1_o3, bcd_adder_1_o2, bcd_adder_1_o1, bcd_adder_1_o0}),
    .in1({bcd_subtractor_1_o7, bcd_subtractor_1_o6, bcd_subtractor_1_o5, bcd_subtractor_1_o4, bcd_subtractor_1_o3, bcd_subtractor_1_o2, bcd_subtractor_1_o1, bcd_subtractor_1_o0}),
    .in2({bcd_multiplication_1_o7, bcd_multiplication_1_o6, bcd_multiplication_1_o5, bcd_multiplication_1_o4, bcd_multiplication_1_o3, bcd_multiplication_1_o2, bcd_multiplication_1_o1, bcd_multiplication_1_o0}),
    .in3({bcd_division_1_o7, bcd_division_1_o6, bcd_division_1_o5, bcd_division_1_o4, bcd_division_1_o3, bcd_division_1_o2, bcd_division_1_o1, bcd_division_1_o0}),
    .out({O7, O6, O5, O4, O3, O2, O1, O0}), .sel(and_3_out), .en(or_32_out));
  or or_31 (and_3_out[1], MULTIPLICATION, DIVISION);
  Multiplexer #(.width(16)) multiplexer_2 (
    .in1({bcd_division_1_r3, bcd_division_1_r2, bcd_division_1_r1, bcd_division_1_r0}),
    .out({R3, R2, R1, R0}), .sel(DIVISION));  // open: in0, en
  and and_3 (and_3_out[0], not_1_out, not_2_out);
  not not_1 (not_1_out, ADDITION);
  not not_2 (not_2_out, MULTIPLICATION);
  or or_32 (or_32_out, MULTIPLICATION, DIVISION, ADDITION, SUBTRACTION);

  // Other names for the same wires on the sheet: bit0_m[3:0] = {_3m[0], _2m[0], _1m[0], _0m[0]};
  //   bit1_m[3:0] = {_3m[1], _2m[1], _1m[1], _0m[1]}; bit2_m[3:0] = {_3m[2], _2m[2], _1m[2], _0m[2]};
  //   bit3_m[3:0] = {_3m[3], _2m[3], _1m[3], _0m[3]}; bit0[3:0] = {_3n[0], _2n[0], _1n[0], _0n[0]};
  //   bit1[3:0] = {_3n[1], _2n[1], _1n[1], _0n[1]}; bit2[3:0] = {_3n[2], _2n[2], _1n[2], _0n[2]};
  //   bit3[3:0] = {_3n[3], _2n[3], _1n[3], _0n[3]}; LEFT_RIGHT = Backspace; LEFT_RIGHT_m = Backspace_m;
  //   tunnel = MULTIPLICATION; tunnel_t = ADDITION; tunnel_t_t = SUBTRACTION; tunnel_t_t_t = DIVISION

  // Notes on the sheet:
  //   TAKING INPUTS -
  //   BCD Representation -
  //   Making the 12 Digit Display -
  //   For BCD representation, we need 4 bits (to uniquely represent every number from 0 through 9)
  //   The trick was to make the T flip flop rising edge triggered while the
  //   left right shift register is falling edge triggered! (24/12/2011 6:46PM A'bad)
  //   This small OR gate prevents adding
  //   more digits when the 12th bit is non zero
  //    (12 bits - 0 through 11)
  //   This small OR gate prevents adding
  //   more digits when the 12th bit is non zero
  //   ADDER
  //   SEBTRACTER
  //                              MULTIPLIER
  //   DIVIDER
endmodule

module l_r_shift (
  input  right_left_shift,
  input  Data_In_Right_Shift,
  input  Data_In_Left_Shift,
  input  CLK,
  input  RESET,
  output [3:0] Current_State_of_Registers,
  output Data_out_Right_Shift,
  output Data_Out_Left_Shift
);

  wire and_1_out, and_2_out, and_3_out, and_4_out, and_5_out, and_6_out, and_7_out, and_8_out, not_1_out,
       or_1_out, or_2_out, or_3_out, or_4_out;

  not not_1 (not_1_out, right_left_shift);
  and and_1 (and_1_out, Current_State_of_Registers[1], right_left_shift);
  or or_1 (or_1_out, and_1_out, and_2_out);
  and and_2 (and_2_out, Data_In_Right_Shift, not_1_out);
  D_Flip_Flop #(.trigger("falling")) LSB (
    .clk(CLK), .D(or_1_out), .Q(Current_State_of_Registers[0]), .reset(RESET));  // open: Qn, preset, en
  and and_3 (and_3_out, Current_State_of_Registers[2], right_left_shift);
  and and_4 (and_4_out, Current_State_of_Registers[0], not_1_out);
  D_Flip_Flop #(.trigger("falling")) d_ff_1 (
    .clk(CLK), .D(or_2_out), .Q(Current_State_of_Registers[1]), .reset(RESET));  // open: Qn, preset, en
  or or_2 (or_2_out, and_3_out, and_4_out);
  and and_5 (and_5_out, Current_State_of_Registers[3], right_left_shift);
  and and_6 (and_6_out, Current_State_of_Registers[1], not_1_out);
  or or_3 (or_3_out, and_5_out, and_6_out);
  D_Flip_Flop #(.trigger("falling")) d_ff_2 (
    .clk(CLK), .D(or_3_out), .Q(Current_State_of_Registers[2]), .reset(RESET));  // open: Qn, preset, en
  and and_7 (and_7_out, Data_In_Left_Shift, right_left_shift);
  or or_4 (or_4_out, and_7_out, and_8_out);
  and and_8 (and_8_out, Current_State_of_Registers[2], not_1_out);
  D_Flip_Flop #(.trigger("falling")) MSB (
    .clk(CLK), .D(or_4_out), .Q(Current_State_of_Registers[3]), .reset(RESET));  // open: Qn, preset, en

  assign Data_Out_Left_Shift = Current_State_of_Registers[0];
  assign Data_out_Right_Shift = Current_State_of_Registers[3];

  // Notes on the sheet:
  //   4 bit left right shift register
endmodule

// Shift
module _12_bit_left_right_shift_register (
  input  Data_in_right_shift,
  input  right_left_shift,
  input  CLK,
  input  RESET,
  output [11:0] Current_State__12_bits
);

  wire l_r_shift_1_data_out_left_shift, l_r_shift_1_data_out_right_shift, LSB_data_out_right_shift,
       MSB_data_out_left_shift;

  l_r_shift LSB (
    .Current_State_of_Registers(Current_State__12_bits[3:0]), .right_left_shift(right_left_shift),
    .Data_In_Right_Shift(Data_in_right_shift), .CLK(CLK),
    .Data_In_Left_Shift(l_r_shift_1_data_out_left_shift), .Data_out_Right_Shift(LSB_data_out_right_shift),
    .RESET(RESET));  // open: Data_Out_Left_Shift
  l_r_shift l_r_shift_1 (
    .Current_State_of_Registers(Current_State__12_bits[7:4]), .right_left_shift(right_left_shift),
    .Data_In_Right_Shift(LSB_data_out_right_shift), .CLK(CLK), .Data_In_Left_Shift(MSB_data_out_left_shift),
    .Data_out_Right_Shift(l_r_shift_1_data_out_right_shift),
    .Data_Out_Left_Shift(l_r_shift_1_data_out_left_shift), .RESET(RESET));
  l_r_shift MSB (
    .Current_State_of_Registers(Current_State__12_bits[11:8]), .right_left_shift(right_left_shift),
    .Data_In_Right_Shift(l_r_shift_1_data_out_right_shift), .CLK(CLK), .Data_In_Left_Shift(1'b0),
    .Data_Out_Left_Shift(MSB_data_out_left_shift), .RESET(RESET));  // open: Data_out_Right_Shift

  // Notes on the sheet:
  //   Current_State__12_bits: pull=up
endmodule

module BCD_ADIITION (
  input  cin,
  input  [3:0] input_1,
  input  [3:0] input_2,
  output [3:0] sum,
  output c_out
);

  wire adder_1_cout, adder_2_cout, and_1_out, and_2_out;
  wire [2:2] or_1_out;
  wire [3:0] adder_1_out;

  Adder #(.width(4)) adder_1 (.a(input_1), .b(input_2), .out(adder_1_out), .cin(cin), .cout(adder_1_cout));
  and and_1 (and_1_out, adder_1_out[1], adder_1_out[3]);
  and and_2 (and_2_out, adder_1_out[2], adder_1_out[3]);
  or or_1 (or_1_out[2], and_1_out, and_2_out, adder_1_cout);
  Adder #(.width(4)) adder_2 (
    .a(adder_1_out), .b({1'b0, {2{or_1_out[2]}}, 1'b0}), .out(sum), .cout(adder_2_cout));  // open: cin
  or or_2 (c_out, adder_2_cout, adder_1_cout);
endmodule

module bcd_adder_and_subtractor (
  input  cin,
  input  [3:0] input_1,
  input  [3:0] input_2,
  input  mode,
  output [3:0] out,
  output c_out
);

  wire [3:0] multiplexer_1_out, n9_s_compliment_1_out_2;

  _9_s_compliment u_9_s_compliment_1 (.in_1(input_2), .out_2(n9_s_compliment_1_out_2));
  Multiplexer #(.width(4)) multiplexer_1 (
    .in0(input_2), .in1(n9_s_compliment_1_out_2), .out(multiplexer_1_out), .sel(mode));  // open: en
  BCD_ADIITION bcd_adiition_1 (.cin(cin), .input_1(input_1), .input_2(multiplexer_1_out), .sum(out), .c_out(c_out));
endmodule

module _9_s_compliment (
  input  [3:0] in_1,
  output [3:0] out_2
);

  Subtractor #(.width(4)) subtractor_1 (.a(4'b1001), .b(in_1), .out(out_2));  // open: bin, bout
endmodule

module multiplication (
  input  [3:0] in_1,
  input  [3:0] in_2,
  output [3:0] car,
  output [3:0] ans
);

  wire [3:0] multiplier_1_cout, multiplier_1_out;
  wire [7:4] divider_1_out, divider_1_rem;

  Multiplier #(.width(4)) multiplier_1 (
    .a(in_1), .b(in_2), .out(multiplier_1_out), .cout(multiplier_1_cout));  // open: cin
  Divider divider_1 (
    .a({multiplier_1_cout, multiplier_1_out}), .b(8'ha), .out({divider_1_out, car}),
    .rem({divider_1_rem, ans}));  // open: upper
endmodule

module _4_bit_multiplication (
  input  [3:0] x0,
  input  [3:0] x1,
  input  [3:0] x2,
  input  [3:0] x3,
  input  [3:0] y0,
  input  [3:0] y1,
  input  [3:0] y2,
  input  [3:0] y3,
  output [3:0] x0y0,
  output [3:0] x1y0,
  output [3:0] x2y0,
  output [3:0] x3y0,
  output [3:0] c0,
  output [3:0] x0y1,
  output [3:0] x1y1,
  output [3:0] x2y1,
  output [3:0] x3y1,
  output [3:0] c1,
  output [3:0] x0y2,
  output [3:0] x1y2,
  output [3:0] x2y2,
  output [3:0] x3y2,
  output [3:0] c2,
  output [3:0] x0y3,
  output [3:0] x1y3,
  output [3:0] x2y3,
  output [3:0] x3y3,
  output [3:0] c3
);

  wire [0:0] bcd_adiition_1_c_out, bcd_adiition_3_c_out, bcd_adiition_5_c_out, bcd_adiition_7_c_out,
       bcd_adiition_9_c_out, bcd_adiition_11_c_out, bcd_adiition_13_c_out, bcd_adiition_15_c_out,
       bcd_adiition_17_c_out, bcd_adiition_19_c_out, bcd_adiition_21_c_out, bcd_adiition_23_c_out;
  wire [3:0] bcd_adiition_2_sum, bcd_adiition_4_sum, bcd_adiition_8_sum, bcd_adiition_10_sum,
       bcd_adiition_14_sum, bcd_adiition_16_sum, bcd_adiition_20_sum, bcd_adiition_22_sum,
       multiplication_1_car, multiplication_2_ans, multiplication_2_car, multiplication_3_ans,
       multiplication_3_car, multiplication_4_ans, multiplication_4_car, multiplication_5_car,
       multiplication_6_ans, multiplication_6_car, multiplication_7_ans, multiplication_7_car,
       multiplication_8_ans, multiplication_8_car, multiplication_9_car, multiplication_10_ans,
       multiplication_10_car, multiplication_11_ans, multiplication_11_car, multiplication_12_ans,
       multiplication_12_car, multiplication_13_car, multiplication_14_ans, multiplication_14_car,
       multiplication_15_ans, multiplication_15_car, multiplication_16_ans, multiplication_16_car;

  multiplication multiplication_1 (.in_1(y0), .in_2(x0), .car(multiplication_1_car), .ans(x0y0));
  multiplication multiplication_2 (.in_1(y0), .in_2(x1), .car(multiplication_2_car), .ans(multiplication_2_ans));
  multiplication multiplication_3 (.in_1(y0), .in_2(x2), .car(multiplication_3_car), .ans(multiplication_3_ans));
  multiplication multiplication_4 (.in_1(y0), .in_2(x3), .car(multiplication_4_car), .ans(multiplication_4_ans));
  BCD_ADIITION bcd_adiition_1 (
    .input_1(multiplication_1_car), .input_2(multiplication_2_ans), .sum(x1y0),
    .c_out(bcd_adiition_1_c_out[0]));  // open: cin
  BCD_ADIITION bcd_adiition_2 (
    .input_1({3'b000, bcd_adiition_1_c_out[0]}), .input_2(multiplication_2_car), .sum(bcd_adiition_2_sum));  // open: cin, c_out
  BCD_ADIITION bcd_adiition_3 (
    .input_1(bcd_adiition_2_sum), .input_2(multiplication_3_ans), .sum(x2y0), .c_out(bcd_adiition_3_c_out[0]));  // open: cin
  BCD_ADIITION bcd_adiition_4 (
    .input_1({3'b000, bcd_adiition_3_c_out[0]}), .input_2(multiplication_3_car), .sum(bcd_adiition_4_sum));  // open: cin, c_out
  BCD_ADIITION bcd_adiition_5 (
    .input_1(bcd_adiition_4_sum), .input_2(multiplication_4_ans), .sum(x3y0), .c_out(bcd_adiition_5_c_out[0]));  // open: cin
  BCD_ADIITION bcd_adiition_6 (
    .input_1({3'b000, bcd_adiition_5_c_out[0]}), .input_2(multiplication_4_car), .sum(c0));  // open: cin, c_out
  multiplication multiplication_5 (.in_1(y1), .in_2(x0), .car(multiplication_5_car), .ans(x0y1));
  multiplication multiplication_6 (.in_1(y1), .in_2(x1), .car(multiplication_6_car), .ans(multiplication_6_ans));
  multiplication multiplication_7 (.in_1(y1), .in_2(x2), .car(multiplication_7_car), .ans(multiplication_7_ans));
  multiplication multiplication_8 (.in_1(y1), .in_2(x3), .car(multiplication_8_car), .ans(multiplication_8_ans));
  BCD_ADIITION bcd_adiition_7 (
    .input_1(multiplication_5_car), .input_2(multiplication_6_ans), .sum(x1y1),
    .c_out(bcd_adiition_7_c_out[0]));  // open: cin
  BCD_ADIITION bcd_adiition_8 (
    .input_1({3'b000, bcd_adiition_7_c_out[0]}), .input_2(multiplication_6_car), .sum(bcd_adiition_8_sum));  // open: cin, c_out
  BCD_ADIITION bcd_adiition_9 (
    .input_1(bcd_adiition_8_sum), .input_2(multiplication_7_ans), .sum(x2y1), .c_out(bcd_adiition_9_c_out[0]));  // open: cin
  BCD_ADIITION bcd_adiition_10 (
    .input_1({3'b000, bcd_adiition_9_c_out[0]}), .input_2(multiplication_7_car), .sum(bcd_adiition_10_sum));  // open: cin, c_out
  BCD_ADIITION bcd_adiition_11 (
    .input_1(bcd_adiition_10_sum), .input_2(multiplication_8_ans), .sum(x3y1),
    .c_out(bcd_adiition_11_c_out[0]));  // open: cin
  BCD_ADIITION bcd_adiition_12 (
    .input_1({3'b000, bcd_adiition_11_c_out[0]}), .input_2(multiplication_8_car), .sum(c1));  // open: cin, c_out
  multiplication multiplication_9 (.in_1(y2), .in_2(x0), .car(multiplication_9_car), .ans(x0y2));
  multiplication multiplication_10 (.in_1(y2), .in_2(x1), .car(multiplication_10_car), .ans(multiplication_10_ans));
  multiplication multiplication_11 (.in_1(y2), .in_2(x2), .car(multiplication_11_car), .ans(multiplication_11_ans));
  multiplication multiplication_12 (.in_1(y2), .in_2(x3), .car(multiplication_12_car), .ans(multiplication_12_ans));
  BCD_ADIITION bcd_adiition_13 (
    .input_1(multiplication_9_car), .input_2(multiplication_10_ans), .sum(x1y2),
    .c_out(bcd_adiition_13_c_out[0]));  // open: cin
  BCD_ADIITION bcd_adiition_14 (
    .input_1({3'b000, bcd_adiition_13_c_out[0]}), .input_2(multiplication_10_car), .sum(bcd_adiition_14_sum));  // open: cin, c_out
  BCD_ADIITION bcd_adiition_15 (
    .input_1(bcd_adiition_14_sum), .input_2(multiplication_11_ans), .sum(x2y2),
    .c_out(bcd_adiition_15_c_out[0]));  // open: cin
  BCD_ADIITION bcd_adiition_16 (
    .input_1({3'b000, bcd_adiition_15_c_out[0]}), .input_2(multiplication_11_car), .sum(bcd_adiition_16_sum));  // open: cin, c_out
  BCD_ADIITION bcd_adiition_17 (
    .input_1(bcd_adiition_16_sum), .input_2(multiplication_12_ans), .sum(x3y2),
    .c_out(bcd_adiition_17_c_out[0]));  // open: cin
  BCD_ADIITION bcd_adiition_18 (
    .input_1({3'b000, bcd_adiition_17_c_out[0]}), .input_2(multiplication_12_car), .sum(c2));  // open: cin, c_out
  multiplication multiplication_13 (.in_1(y3), .in_2(x0), .car(multiplication_13_car), .ans(x0y3));
  multiplication multiplication_14 (.in_1(y3), .in_2(x1), .car(multiplication_14_car), .ans(multiplication_14_ans));
  multiplication multiplication_15 (.in_1(y3), .in_2(x2), .car(multiplication_15_car), .ans(multiplication_15_ans));
  multiplication multiplication_16 (.in_1(y3), .in_2(x3), .car(multiplication_16_car), .ans(multiplication_16_ans));
  BCD_ADIITION bcd_adiition_19 (
    .input_1(multiplication_13_car), .input_2(multiplication_14_ans), .sum(x1y3),
    .c_out(bcd_adiition_19_c_out[0]));  // open: cin
  BCD_ADIITION bcd_adiition_20 (
    .input_1({3'b000, bcd_adiition_19_c_out[0]}), .input_2(multiplication_14_car), .sum(bcd_adiition_20_sum));  // open: cin, c_out
  BCD_ADIITION bcd_adiition_21 (
    .input_1(bcd_adiition_20_sum), .input_2(multiplication_15_ans), .sum(x2y3),
    .c_out(bcd_adiition_21_c_out[0]));  // open: cin
  BCD_ADIITION bcd_adiition_22 (
    .input_1({3'b000, bcd_adiition_21_c_out[0]}), .input_2(multiplication_15_car), .sum(bcd_adiition_22_sum));  // open: cin, c_out
  BCD_ADIITION bcd_adiition_23 (
    .input_1(bcd_adiition_22_sum), .input_2(multiplication_16_ans), .sum(x3y3),
    .c_out(bcd_adiition_23_c_out[0]));  // open: cin
  BCD_ADIITION bcd_adiition_24 (
    .input_1({3'b000, bcd_adiition_23_c_out[0]}), .input_2(multiplication_16_car), .sum(c3));  // open: cin, c_out
endmodule

module bcd_to_binary (
  input  [3:0] IN0,
  input  [3:0] IN1,
  input  [3:0] IN2,
  input  [3:0] IN3,
  output [31:0] OUT
);

  wire [3:0] multiplier_1_cout, multiplier_1_out, multiplier_2_cout, multiplier_2_out, multiplier_3_cout,
       multiplier_3_out;
  wire [7:0] adder_1_out, multiplier_4_cout, multiplier_4_out, multiplier_5_cout, multiplier_5_out;
  wire [15:0] adder_2_out, multiplier_6_cout, multiplier_6_out;

  Multiplier #(.width(4)) multiplier_1 (
    .a(IN3), .b(4'b1010), .out(multiplier_1_out), .cout(multiplier_1_cout));  // open: cin
  Multiplier #(.width(4)) multiplier_2 (
    .a(IN1), .b(4'b1010), .out(multiplier_2_out), .cout(multiplier_2_cout));  // open: cin
  Multiplier #(.width(4)) multiplier_3 (
    .a(IN2), .b(4'b1010), .out(multiplier_3_out), .cout(multiplier_3_cout));  // open: cin
  Adder adder_1 (.a({4'b0000, IN0}), .b({multiplier_2_cout, multiplier_2_out}), .out(adder_1_out));  // open: cin, cout
  Multiplier multiplier_4 (
    .a({multiplier_1_cout, multiplier_1_out}), .b(8'ha), .out(multiplier_4_out), .cout(multiplier_4_cout));  // open: cin
  Multiplier multiplier_5 (
    .a({multiplier_3_cout, multiplier_3_out}), .b(8'ha), .out(multiplier_5_out), .cout(multiplier_5_cout));  // open: cin
  Adder #(.width(16)) adder_2 (
    .a({{8{1'b0}}, adder_1_out}), .b({multiplier_5_cout, multiplier_5_out}), .out(adder_2_out));  // open: cin, cout
  Multiplier #(.width(16)) multiplier_6 (
    .a({multiplier_4_cout, multiplier_4_out}), .b(16'ha), .out(multiplier_6_out), .cout(multiplier_6_cout));  // open: cin
  Adder #(.width(32)) adder_3 (
    .a({{16{1'b0}}, adder_2_out}), .b({multiplier_6_cout, multiplier_6_out}), .out(OUT));  // open: cin, cout
endmodule

module BCD_subtractor (
  input  [3:0] _0n,
  input  [3:0] _1n,
  input  [3:0] _2n,
  input  [3:0] _3n,
  input  [3:0] _0m,
  input  [3:0] _1m,
  input  [3:0] _2m,
  input  [3:0] _3m,
  output [3:0] O0,
  output [3:0] O1,
  output [3:0] O2,
  output [3:0] O3,
  output [3:0] O4,
  output [3:0] O5,
  output [3:0] O6,
  output [3:0] O7
);

  wire bcd_adder_and_subtractor_1_c_out, bcd_adder_and_subtractor_2_c_out, bcd_adder_and_subtractor_3_c_out;

  bcd_adder_and_subtractor bcd_adder_and_subtractor_1 (
    .cin(1'b1), .input_1(_0n), .input_2(_0m), .mode(1'b1), .out(O0), .c_out(bcd_adder_and_subtractor_1_c_out));
  bcd_adder_and_subtractor bcd_adder_and_subtractor_2 (
    .cin(bcd_adder_and_subtractor_1_c_out), .input_1(_1n), .input_2(_1m), .mode(1'b1), .out(O1),
    .c_out(bcd_adder_and_subtractor_2_c_out));
  bcd_adder_and_subtractor bcd_adder_and_subtractor_3 (
    .cin(bcd_adder_and_subtractor_2_c_out), .input_1(_2n), .input_2(_2m), .mode(1'b1), .out(O2),
    .c_out(bcd_adder_and_subtractor_3_c_out));
  bcd_adder_and_subtractor bcd_adder_and_subtractor_4 (
    .cin(bcd_adder_and_subtractor_3_c_out), .input_1(_3n), .input_2(_3m), .mode(1'b1), .out(O3));  // open: c_out

  assign O4 = 4'b0000;
  assign O5 = 4'b0000;
  assign O6 = 4'b0000;
  assign O7 = 4'b0000;
endmodule

module BCD_multiplication (
  input  [3:0] _0n,
  input  [3:0] _1n,
  input  [3:0] _2n,
  input  [3:0] _3n,
  input  [3:0] _0m,
  input  [3:0] _1m,
  input  [3:0] _2m,
  input  [3:0] _3m,
  output [3:0] O0,
  output [3:0] O1,
  output [3:0] O2,
  output [3:0] O3,
  output [3:0] O4,
  output [3:0] O5,
  output [3:0] O6,
  output [3:0] O7
);

  wire bcd_adiition_1_c_out, bcd_adiition_2_c_out, bcd_adiition_3_c_out, bcd_adiition_4_c_out,
       bcd_adiition_5_c_out, bcd_adiition_6_c_out, bcd_adiition_7_c_out, bcd_adiition_8_c_out,
       bcd_adiition_9_c_out, bcd_adiition_11_c_out, bcd_adiition_12_c_out, bcd_adiition_13_c_out;
  wire [0:0] bcd_adiition_10_c_out, bcd_adiition_14_c_out;
  wire [3:0] bcd_adiition_2_sum, bcd_adiition_4_sum, bcd_adiition_5_sum, bcd_adiition_7_sum,
       bcd_adiition_8_sum, bcd_adiition_11_sum, bcd_adiition_13_sum, bcd_adiition_14_sum,
       n4_bit_multiplication_1_c0, n4_bit_multiplication_1_c1, n4_bit_multiplication_1_c2,
       n4_bit_multiplication_1_c3, n4_bit_multiplication_1_x0y1, n4_bit_multiplication_1_x0y2,
       n4_bit_multiplication_1_x0y3, n4_bit_multiplication_1_x1y0, n4_bit_multiplication_1_x1y1,
       n4_bit_multiplication_1_x1y2, n4_bit_multiplication_1_x1y3, n4_bit_multiplication_1_x2y0,
       n4_bit_multiplication_1_x2y1, n4_bit_multiplication_1_x2y2, n4_bit_multiplication_1_x2y3,
       n4_bit_multiplication_1_x3y0, n4_bit_multiplication_1_x3y1, n4_bit_multiplication_1_x3y2,
       n4_bit_multiplication_1_x3y3;

  _4_bit_multiplication u_4_bit_multiplication_1 (
    .x0(_0n), .x1(_1n), .x2(_2n), .x3(_3n), .y0(_0m), .y1(_1m), .y2(_2m), .y3(_3m), .x0y0(O0),
    .x1y0(n4_bit_multiplication_1_x1y0), .x2y0(n4_bit_multiplication_1_x2y0),
    .x3y0(n4_bit_multiplication_1_x3y0), .c0(n4_bit_multiplication_1_c0),
    .x0y1(n4_bit_multiplication_1_x0y1), .x1y1(n4_bit_multiplication_1_x1y1),
    .x2y1(n4_bit_multiplication_1_x2y1), .x3y1(n4_bit_multiplication_1_x3y1),
    .c1(n4_bit_multiplication_1_c1), .x0y2(n4_bit_multiplication_1_x0y2),
    .x1y2(n4_bit_multiplication_1_x1y2), .x2y2(n4_bit_multiplication_1_x2y2),
    .x3y2(n4_bit_multiplication_1_x3y2), .c2(n4_bit_multiplication_1_c2),
    .x0y3(n4_bit_multiplication_1_x0y3), .x1y3(n4_bit_multiplication_1_x1y3),
    .x2y3(n4_bit_multiplication_1_x2y3), .x3y3(n4_bit_multiplication_1_x3y3), .c3(n4_bit_multiplication_1_c3));
  BCD_ADIITION bcd_adiition_1 (
    .input_1(n4_bit_multiplication_1_x1y0), .input_2(n4_bit_multiplication_1_x0y1), .sum(O1),
    .c_out(bcd_adiition_1_c_out));  // open: cin
  BCD_ADIITION bcd_adiition_2 (
    .cin(bcd_adiition_1_c_out), .input_1(n4_bit_multiplication_1_x1y1),
    .input_2(n4_bit_multiplication_1_x2y0), .sum(bcd_adiition_2_sum), .c_out(bcd_adiition_2_c_out));
  BCD_ADIITION bcd_adiition_3 (
    .input_1(bcd_adiition_2_sum), .input_2(n4_bit_multiplication_1_x0y2), .sum(O2),
    .c_out(bcd_adiition_3_c_out));  // open: cin
  BCD_ADIITION bcd_adiition_4 (
    .cin(bcd_adiition_2_c_out), .input_1(n4_bit_multiplication_1_x3y0),
    .input_2(n4_bit_multiplication_1_x2y1), .sum(bcd_adiition_4_sum), .c_out(bcd_adiition_4_c_out));
  BCD_ADIITION bcd_adiition_5 (
    .cin(bcd_adiition_3_c_out), .input_1(bcd_adiition_4_sum), .input_2(n4_bit_multiplication_1_x1y2),
    .sum(bcd_adiition_5_sum), .c_out(bcd_adiition_5_c_out));
  BCD_ADIITION bcd_adiition_6 (
    .input_1(bcd_adiition_5_sum), .input_2(n4_bit_multiplication_1_x0y3), .sum(O3),
    .c_out(bcd_adiition_6_c_out));  // open: cin
  BCD_ADIITION bcd_adiition_7 (
    .cin(bcd_adiition_5_c_out), .input_1(bcd_adiition_8_sum), .input_2(n4_bit_multiplication_1_x2y2),
    .sum(bcd_adiition_7_sum), .c_out(bcd_adiition_7_c_out));
  BCD_ADIITION bcd_adiition_8 (
    .cin(bcd_adiition_4_c_out), .input_1(n4_bit_multiplication_1_c0), .input_2(n4_bit_multiplication_1_x3y1),
    .sum(bcd_adiition_8_sum), .c_out(bcd_adiition_8_c_out));
  BCD_ADIITION bcd_adiition_9 (
    .cin(bcd_adiition_6_c_out), .input_1(bcd_adiition_7_sum), .input_2(n4_bit_multiplication_1_x1y3),
    .sum(O4), .c_out(bcd_adiition_9_c_out));
  BCD_ADIITION bcd_adiition_10 (
    .cin(bcd_adiition_9_c_out), .input_1(4'b0000), .input_2(bcd_adiition_13_sum), .sum(O5),
    .c_out(bcd_adiition_10_c_out[0]));
  BCD_ADIITION bcd_adiition_11 (
    .cin(bcd_adiition_8_c_out), .input_1(n4_bit_multiplication_1_c1), .input_2(n4_bit_multiplication_1_x3y2),
    .sum(bcd_adiition_11_sum), .c_out(bcd_adiition_11_c_out));
  BCD_ADIITION bcd_adiition_12 (
    .cin(bcd_adiition_13_c_out), .input_1({3'b000, bcd_adiition_10_c_out[0]}), .input_2(bcd_adiition_14_sum),
    .sum(O6), .c_out(bcd_adiition_12_c_out));
  BCD_ADIITION bcd_adiition_13 (
    .cin(bcd_adiition_7_c_out), .input_1(bcd_adiition_11_sum), .input_2(n4_bit_multiplication_1_x2y3),
    .sum(bcd_adiition_13_sum), .c_out(bcd_adiition_13_c_out));
  BCD_ADIITION bcd_adiition_14 (
    .cin(bcd_adiition_11_c_out), .input_1(n4_bit_multiplication_1_x3y3),
    .input_2(n4_bit_multiplication_1_c2), .sum(bcd_adiition_14_sum), .c_out(bcd_adiition_14_c_out[0]));
  BCD_ADIITION bcd_adiition_15 (
    .cin(bcd_adiition_12_c_out), .input_1(n4_bit_multiplication_1_c3),
    .input_2({3'b000, bcd_adiition_14_c_out[0]}), .sum(O7));  // open: c_out
endmodule

module BCD_Adder (
  input  [3:0] _0n,
  input  [3:0] _1n,
  input  [3:0] _2n,
  input  [3:0] _3n,
  input  [3:0] _0m,
  input  [3:0] _1m,
  input  [3:0] _2m,
  input  [3:0] _3m,
  output [3:0] O0,
  output [3:0] O1,
  output [3:0] O2,
  output [3:0] O3,
  output [3:0] O4,
  output [3:0] O5,
  output [3:0] O6,
  output [3:0] O7
);

  wire bcd_adiition_1_c_out, bcd_adiition_2_c_out, bcd_adiition_3_c_out;

  BCD_ADIITION bcd_adiition_1 (.input_1(_0n), .input_2(_0m), .sum(O0), .c_out(bcd_adiition_1_c_out));  // open: cin
  BCD_ADIITION bcd_adiition_2 (
    .cin(bcd_adiition_1_c_out), .input_1(_1n), .input_2(_1m), .sum(O1), .c_out(bcd_adiition_2_c_out));
  BCD_ADIITION bcd_adiition_3 (
    .cin(bcd_adiition_2_c_out), .input_1(_2n), .input_2(_2m), .sum(O2), .c_out(bcd_adiition_3_c_out));
  BCD_ADIITION bcd_adiition_4 (.cin(bcd_adiition_3_c_out), .input_1(_3n), .input_2(_3m), .sum(O3), .c_out(O4[0]));

  assign O4[3:1] = 3'b000;
  assign O5 = 4'b0000;
  assign O6 = 4'b0000;
  assign O7 = 4'b0000;
endmodule

module BCD_division (
  input  [3:0] _0n,
  input  [3:0] _1n,
  input  [3:0] _2n,
  input  [3:0] _3n,
  input  [3:0] _0m,
  input  [3:0] _1m,
  input  [3:0] _2m,
  input  [3:0] _3m,
  output [3:0] O0,
  output [3:0] O1,
  output [3:0] O2,
  output [3:0] O3,
  output [3:0] O4,
  output [3:0] O5,
  output [3:0] O6,
  output [3:0] O7,
  output [3:0] R0,
  output [3:0] R1,
  output [3:0] R2,
  output [3:0] R3
);

  wire [3:0] divider_5_rem, divider_6_rem, divider_6_rem_2;
  wire [15:0] divider_2_out, divider_3_out, divider_4_out, divider_5_out, divider_6_out, divider_8_out;
  wire [15:4] divider_2_rem, divider_3_rem, divider_4_rem, divider_7_rem, divider_8_rem, divider_9_rem;
  wire [15:8] divider_5_rem_2;
  wire [15:12] divider_6_rem_3;
  wire [31:0] bcd_to_binary_1_out, bcd_to_binary_2_out, divider_1_out, divider_1_rem;

  bcd_to_binary bcd_to_binary_1 (.IN0(_0n), .IN1(_1n), .IN2(_2n), .IN3(_3n), .OUT(bcd_to_binary_1_out));
  bcd_to_binary bcd_to_binary_2 (.IN0(_0m), .IN1(_1m), .IN2(_2m), .IN3(_3m), .OUT(bcd_to_binary_2_out));
  Divider #(.width(32)) divider_1 (
    .a(bcd_to_binary_1_out), .b(bcd_to_binary_2_out), .out(divider_1_out), .rem(divider_1_rem));  // open: upper
  Divider #(.width(16)) divider_2 (
    .a(divider_1_rem[15:0]), .b(16'ha), .out(divider_2_out), .rem({divider_2_rem, R0}));  // open: upper
  Divider #(.width(16)) divider_3 (
    .a(divider_1_out[15:0]), .b(16'ha), .out(divider_3_out), .rem({divider_3_rem, O0}));  // open: upper
  Divider #(.width(16)) divider_4 (
    .a(divider_2_out), .b(16'ha), .out(divider_4_out), .rem({divider_4_rem, R1}));  // open: upper
  Divider #(.width(16)) divider_5 (
    .a(divider_3_out), .b(16'ha), .out(divider_5_out), .rem({divider_5_rem_2, divider_5_rem, O1}));  // open: upper
  Divider #(.width(16)) divider_6 (
    .a(divider_4_out), .b(16'ha), .out(divider_6_out),
    .rem({divider_6_rem_3, divider_6_rem_2, divider_6_rem, R2}));  // open: upper
  Divider #(.width(16)) divider_7 (.a(divider_6_out), .b(16'ha), .rem({divider_7_rem, R3}));  // open: out, upper
  Divider #(.width(16)) divider_8 (
    .a(divider_5_out), .b(16'ha), .out(divider_8_out), .rem({divider_8_rem, O2}));  // open: upper
  Divider #(.width(16)) divider_9 (.a(divider_8_out), .b(16'ha), .rem({divider_9_rem, O3}));  // open: out, upper

  assign O4 = 4'b0000;
  assign O5 = 4'b0000;
  assign O6 = 4'b0000;
  assign O7 = 4'b0000;
endmodule
